// Logisim project bistabile.circ as structural Verilog: 7 circuits, main circuit main
module main (
  input  R,
  input  S,
  input  s_2,
  input  r_2,
  input  s_3,
  input  r_3,
  input  r_4,
  input  s_4,
  input  R_5,
  input  R_6,
  input  s_5,
  input  S_6,
  input  D,
  input  [3:0] in_14,
  input  w,
  input  [3:0] in_16,
  input  D_2,
  input  R_7,
  input  W_2,
  input  b_t,
  output Q,
  output notQ,
  output out_23,
  output out_24,
  output out_25,
  output q_2,
  output notQ_2,
  output out_28,
  output Q_3,
  output Q_4,
  output notQ_3,
  output notQ_4,
  output Q_5,
  output notQ_5,
  output [3:0] out_35,
  output out_36,
  output [3:0] out_37,
  output [3:0] out_38
);

  wire and_1_out, and_2_out, and_3_out, and_4_out, and_5_out, and_7_out, and_8_out, and_10_out, and_11_out,
       and_12_out, and_13_out, and_14_out, clock_1_out, clock_2_out, clock_3_out, clock_4_out, clock_5_out,
       clock_6_out, clock_7_out, latchd_5_q, not_2_out, not_3_out, or_2_out, r_out, s_out;
  wire [3:0] and_9_out;
  wire [3:3] not_1_out;

  Clock clock_1 (.out(clock_1_out));
  and and_1 (and_1_out, clock_1_out, S_6);
  Clock clock_2 (.out(clock_2_out));
  Clock clock_3 (.out(clock_3_out));
  not not_1 (not_1_out[3], R_7);
  Clock clock_4 (.out(clock_4_out));
  nor nor_1 (Q, R, notQ);
  nor nor_2 (notQ, Q, S);
  and and_2 (and_2_out, ~s_2, ~r_2);  // AND_Gate
  and and_3 (and_3_out, s_2, ~r_2);  // AND_Gate
  and and_4 (and_4_out, ~s_3, ~r_3);  // AND_Gate
  and and_5 (and_5_out, s_3, ~r_3);  // AND_Gate
  or or_1 (out_25, out_28, s_4);
  and and_6 (out_28, out_25, ~r_4);  // AND_Gate
  nor nor_3 (Q_3, and_7_out, notQ_3);
  and and_7 (and_7_out, R_5, clock_1_out);
  nor nor_4 (notQ_3, Q_3, and_1_out);
  and and_8 (and_8_out, clock_2_out, w);
  assign and_9_out = in_16 & {4{not_1_out[3]}};  // AND_Gate and_9, 4 bits wide
  or or_2 (or_2_out, R_7, W_2);
  flip_flop flip_flop_1 (.D(b_t), .in_2(clock_4_out), .out_3(out_38[0]));
  and and_10 (and_10_out, out_23, and_2_out);
  and and_11 (and_11_out, out_24, and_4_out);
  and and_12 (and_12_out, 1'b1, and_5_out);
  latchD latchd_1 (.D(in_14[0]), .in_2(and_8_out), .Q(out_35[0]));  // open: notQ
  latchD latchd_2 (.D(in_14[1]), .in_2(and_8_out), .Q(out_35[1]));  // open: notQ
  latchD latchd_3 (.D(in_14[2]), .in_2(and_8_out), .Q(out_35[2]));  // open: notQ
  latchD latchd_4 (.D(in_14[3]), .in_2(and_8_out), .Q(out_35[3]));  // open: notQ
  flip_flop flip_flop_2 (.D(out_38[0]), .in_2(clock_4_out), .out_3(out_38[1]));
  or or_3 (out_23, and_10_out, and_3_out);
  or or_4 (out_24, and_11_out, and_12_out);
  memoria4bit memoria4bit_1 (.in_1(and_9_out), .clock(clock_3_out), .w(or_2_out), .out_4(out_37));
  flip_flop flip_flop_3 (.D(out_38[1]), .in_2(clock_4_out), .out_3(out_38[2]));
  Clock clock_5 (.out(clock_5_out));
  Clock clock_6 (.out(clock_6_out));
  flip_flop flip_flop_4 (.D(out_38[2]), .in_2(clock_4_out), .out_3(out_38[3]));
  Button u_r (.out(r_out));
  Button u_s (.out(s_out));
  and and_13 (and_13_out, R_6, clock_5_out);
  and and_14 (and_14_out, clock_5_out, s_5);
  not not_2 (not_2_out, D);
  Clock clock_7 (.out(clock_7_out));
  nor nor_5 (q_2, r_out, notQ_2);
  nor nor_6 (notQ_2, q_2, s_out);
  latchASR latchasr_1 (.R(and_13_out), .S(and_14_out), .Q(Q_4), .notQ(notQ_4));
  latchSR latchsr_1 (.R(not_2_out), .clock(clock_6_out), .s(D), .Q(Q_5), .notQ(notQ_5));
  latchD latchd_5 (.D(D_2), .in_2(clock_7_out), .Q(latchd_5_q));  // open: notQ
  not not_3 (not_3_out, clock_7_out);
  latchD latchd_6 (.D(latchd_5_q), .in_2(not_3_out), .Q(out_36));  // open: notQ

  // Other names for the same wires on the sheet: notQ_t = notQ_2; Q_t = q_2

  // Notes on the sheet:
  //   creare uno shfter a 4 bit
  //   AGGIUNGIAMO ORA UN CLOCK
  //   COSTRUIAMO UNA MEMORIA A 4 BIT
  //   COSTRUIRE UNA MEMORIA A 4 BIT CON OPZIONE DI RESET
  //   bistabile asincrono
  //   usiamo ora i tunnel e bottoni
  //   bistabile sincrono
  //   possiamo semplificare ancora
  //   retroazione per cui gli ingressi delle nostre porte logiche
  //   arrivano in momenti diversi
  //   aggiungere una porta in modo che la tt non cambi
  //   USIAMO IL CIRCUITO FATTO PRIMA
  //   prendo in input un valore di write in modo
  //   da andarea a scrivere solo quando c'e il segnale in input
  //   flip-flop usando fue latchD
endmodule

module latchASR (
  input  R,
  input  S,
  output Q,
  output notQ
);

  nor nor_1 (Q, R, notQ);
  nor nor_2 (notQ, Q, S);
endmodule

module latchSR (
  input  R,
  input  clock,
  input  s,
  output Q,
  output notQ
);

  wire and_1_out, and_2_out;

  and and_1 (and_1_out, R, clock);
  and and_2 (and_2_out, clock, s);
  latchASR latchasr_1 (.R(and_1_out), .S(and_2_out), .Q(Q), .notQ(notQ));
endmodule

module latchD (
  input  D,
  input  in_2,
  output Q,
  output notQ
);

  wire not_1_out;

  not not_1 (not_1_out, D);
  latchSR latchsr_1 (.R(not_1_out), .clock(in_2), .s(D), .Q(Q), .notQ(notQ));
endmodule

module memoria4bit (
  input  [3:0] in_1,
  input  clock,
  input  w,
  output [3:0] out_4
);

  wire and_1_out;

  and and_1 (and_1_out, clock, w);
  latchD latchd_1 (.D(in_1[0]), .in_2(and_1_out), .Q(out_4[0]));  // open: notQ
  latchD latchd_2 (.D(in_1[1]), .in_2(and_1_out), .Q(out_4[1]));  // open: notQ
  latchD latchd_3 (.D(in_1[2]), .in_2(and_1_out), .Q(out_4[2]));  // open: notQ
  latchD latchd_4 (.D(in_1[3]), .in_2(and_1_out), .Q(out_4[3]));  // open: notQ
endmodule

module flip_flop (
  input  D,
  input  in_2,
  output out_3
);

  wire latchd_1_q, not_1_out;

  latchD latchd_1 (.D(D), .in_2(in_2), .Q(latchd_1_q));  // open: notQ
  not not_1 (not_1_out, in_2);
  latchD latchd_2 (.D(latchd_1_q), .in_2(not_1_out), .Q(out_3));  // open: notQ
endmodule

module shifter (
  input  b_t,
  input  clock,
  output [3:0] out_3
);

  flip_flop flip_flop_1 (.D(b_t), .in_2(clock), .out_3(out_3[0]));
  flip_flop flip_flop_2 (.D(out_3[0]), .in_2(clock), .out_3(out_3[1]));
  flip_flop flip_flop_3 (.D(out_3[1]), .in_2(clock), .out_3(out_3[2]));
  flip_flop flip_flop_4 (.D(out_3[2]), .in_2(clock), .out_3(out_3[3]));
endmodule
